// Logisim project mata3820171.circ as structural Verilog: 1 circuit, main circuit main
module main (
  input  [3:0] in_1,
  output [1:0] R0,
  output [1:0] R1,
  output [1:0] R2,
  output [1:0] R3,
  output [3:0] out_6,
  output [3:0] out_7,
  output [3:0] out_8,
  output [3:0] out_9,
  output [3:0] out_10,
  output [3:0] out_11,
  output [3:0] out_12,
  output [3:0] out_13,
  output [3:0] out_14,
  output [3:0] out_15,
  output [3:0] out_16,
  output [3:0] out_17,
  output [3:0] out_18,
  output [3:0] out_19,
  output [3:0] out_20,
  output [3:0] out_21
);

  wire [1:0] multiplexer_1_out, multiplexer_2_out;

  Multiplexer #(.select(2), .width(2)) multiplexer_1 (
    .in0(R0), .in1(R1), .in2(R2), .in3(R3), .out(multiplexer_1_out));  // open: sel, en
  Multiplexer #(.select(2), .width(2)) multiplexer_2 (
    .in0(R0), .in1(R1), .in2(R2), .in3(R3), .out(multiplexer_2_out));  // open: sel, en
  Demultiplexer #(.select(4), .width(4)) demultiplexer_1 (
    .out0(out_6), .out1(out_7), .out2(out_8), .out3(out_9), .out4(out_10), .out5(out_11), .out6(out_12),
    .out7(out_13), .out8(out_14), .out9(out_15), .out10(out_16), .out11(out_17), .out12(out_18),
    .out13(out_19), .out14(out_20), .out15(out_21), .in(in_1), .sel(4'b1111));  // open: en
endmodule
